# Fritzing sketch ArduinoMusic (saved by Fritzing 0.9.3b)

parts:
  元件1 = Arduino Nano (Rev3.0)
  LED1 = LED - 5mm [color="White (4500K)" package="5 mm [THT]"]
  LED2 = LED - 5mm [color="White (4500K)" package="5 mm [THT]"]
  LED3 = LED - 5mm [color="White (4500K)" package="5 mm [THT]"]
  LED4 = LED - 5mm [color="White (4500K)" package="5 mm [THT]"]
  LED5 = LED - 5mm [color="White (4500K)" package="5 mm [THT]"]
  LED6 = LED - 5mm [color="White (4500K)" package="5 mm [THT]"]
  LED7 = LED - 5mm [color="White (4500K)" package="5 mm [THT]"]
  LED8 = LED - 5mm [color="White (4500K)" package="5 mm [THT]"]
  LED9 = LED - 5mm [color="White (4500K)" package="5 mm [THT]"]
  LED10 = LED - 5mm [color="White (4500K)" package="5 mm [THT]"]
  LED11 = LED - 5mm [color="White (4500K)" package="5 mm [THT]"]
  LED12 = LED - 5mm [color="White (4500K)" package="5 mm [THT]"]
  SP1 = SPEAKER [package=pcb_mount_speaker]

nets:
  N1: 元件1.D2, LED9.anode
  N2: 元件1.D3, LED12.anode
  N3: 元件1.D4, LED10.anode
  N4: 元件1.D5, LED7.anode
  N5: 元件1.D6, LED5.anode
  N6: 元件1.D7, LED8.anode
  N7: 元件1.D8, LED6.anode
  N8: 元件1.D9, LED3.anode
  N9: 元件1.D10, LED4.anode
  N10: 元件1.D11/MOSI, LED2.anode
  N11: 元件1.D12/MISO, LED1.anode
  N12: 元件1.GND, LED1.cathode, LED2.cathode, LED3.cathode, LED4.cathode, LED5.cathode, LED6.cathode, LED7.cathode, LED8.cathode, LED9.cathode, LED10.cathode, LED11.cathode, LED12.cathode, SP1.+
  N13: 元件1.A2, SP1.-
  N14: 元件1.A0, LED11.anode
