# Fritzing sketch SmartBin (saved by Fritzing 0.9.4)

parts:
  HC-SR04_Sensor_1 = HC-SR04 Ultrasonic Distance Sensor
  元件1 = Arduino Nano (Rev3.0)
  J1 = Basic Servo

nets:
  VCC: HC-SR04_Sensor_1.VCC, 元件1.3V3
  N1: HC-SR04_Sensor_1.TRIG, 元件1.D7
  N2: HC-SR04_Sensor_1.ECHO, 元件1.D6
  GND: HC-SR04_Sensor_1.GND, 元件1.GND, J1.gnd
  N3: 元件1.D8, J1.pulse
  5V: 元件1.5V, J1.vcc
